# Fritzing sketch NTC-Sketch (saved by Fritzing 0.7.7b)
breadboards: 1

parts:
  R13 = Temperature Sensor (Thermistor) [thermistor_type=NTC package=THT]
  R11 = Temperature Sensor (Thermistor) [thermistor_type=NTC package=THT]
  R14 = Resistor [tolerance=±0.1% resistance=470 package=THT]
  R12 = Resistor [tolerance=±0.1% resistance=470 package=THT]
  U1 = Arduino Mega
  Pad1 = Pad [width=7.90222222222222 height=9.03111111111111 connect=center]  # not connected
  Pad2 = Pad [width=7.90222222222222 height=9.03111111111111 connect=center]  # not connected
  Pad3 = Pad [width=7.90222222222222 height=9.03111111111111 connect=center]  # not connected

nets (from the schematic view):
  N1: R13.pin_0, R14.Pin_1, U1.A9
  N2: R13.pin_1, R11.pin_1, U1.+5V
  N3: R11.pin_0, R12.Pin_1, U1.A8
  N4: R14.Pin_0, R12.Pin_0, U1.GND
