# Fritzing sketch NTC_Arduino-Project (saved by Fritzing 0.7.7b)
breadboards: 1

parts:
  Arduino1 = Arduino
  R4 = Resistor [tolerance=±5% resistance=220 package=THT]
  R3 = Temperature Sensor (Thermistor) [thermistor_type=NTC package=THT]  # not connected

nets:
  N1: Arduino1.GND, R4.Pin_1
  N2: Arduino1.A0, R4.Pin_0
